# Fritzing sketch LDR (saved by Fritzing 0.9.3b)
breadboards: 1

parts:
  Componente1 = Arduino Nano (Rev3.0)
  R2 = Resistor [tolerance=±5% resistance=220 package="1206 [SMD]"]
  R3 = Photocell (LDR) [package=THT]
  LED1 = LEDs [package=led10mm]
  R4 = Resistor [tolerance=±5% resistance=220 package="1206 [SMD]"]

nets:
  N1: Componente1.GND, R2.Pin_1, R4.Pin_0
  N2: Componente1.D2, LED1.C
  N3: Componente1.5V, R3.pin_1
  N4: Componente1.A0, R2.Pin_0, R3.pin_0
  N5: LED1.A, R4.Pin_1

// code stored in the sketch: pushbutton.ino

void setup() {
  pinMode(2, INPUT);
  Serial.begin(9600);
}

void loop() {
  // put your main code here, to run repeatedly:
 	int v= digitalRead (2);
  Serial.println(v);
}
