# Fritzing sketch LDR_2 (saved by Fritzing 0.9.3b)
breadboards: 1

parts:
  Componente1 = Arduino Nano (Rev3.0)
  R4 = Resistor [tolerance=±5% resistance=220 package="1206 [SMD]"]
  R5 = Resistor [tolerance=±5% resistance=220 package="1206 [SMD]"]
  R6 = Resistor [tolerance=±5% resistance=220 package="1206 [SMD]"]
  R7 = Resistor [tolerance=±5% resistance=220 package="1206 [SMD]"]
  R8 = Trimmer Potentiometer [maximum_resistance=10kΩ package=THT]
  S1 = Momentary Switch [package=ksa_sealed_tac_switch]
  S2 = Momentary Switch [package=ksa_sealed_tac_switch]
  LED1 = smd LED [color="Red (633nm)" package="1206 [SMD]"]
  LED2 = smd LED [color="Red (633nm)" package="1206 [SMD]"]
  LED3 = smd LED [color="Red (633nm)" package="1206 [SMD]"]
  LED4 = smd LED [color="Red (633nm)" package="1206 [SMD]"]
  LED5 = smd LED [color="Red (633nm)" package="1206 [SMD]"]
  R10 = Resistor [tolerance=±5% resistance=220 package="1206 [SMD]"]
  R11 = Resistor [tolerance=±5% resistance=220 package="1206 [SMD]"]
  R12 = Resistor [tolerance=±5% resistance=220 package="1206 [SMD]"]

nets:
  N1: Componente1.GND, R4.Pin_0, R5.Pin_0, R6.Pin_0, R7.Pin_0, R8.leg1, R10.Pin_0, R11.Pin_0, R12.Pin_0
  N2: Componente1.D2, LED1.cathode
  N3: Componente1.D3, LED2.cathode
  N4: Componente1.D4, LED3.cathode
  N5: Componente1.D5, LED4.cathode
  N6: Componente1.D6, LED5.cathode
  N7: Componente1.5V, R8.leg2, S1.4, S2.4
  N8: Componente1.A2, S1.2, R12.Pin_1
  N9: Componente1.A1, S2.2, R11.Pin_1
  N10: Componente1.A0, R8.wiper
  N11: R4.Pin_1, LED1.anode
  N12: R5.Pin_1, LED2.anode
  N13: R6.Pin_1, LED3.anode
  N14: R7.Pin_1, LED4.anode
  N15: LED5.anode, R10.Pin_1

// code stored in the sketch: pushbutton.ino

void setup() {
  pinMode(2, INPUT);
  Serial.begin(9600);
}

void loop() {
  // put your main code here, to run repeatedly:
 	int v= digitalRead (2);
  Serial.println(v);
}
