# Fritzing sketch pushbutton (saved by Fritzing 0.9.3b)
breadboards: 1

parts:
  Componente1 = Arduino Nano (Rev3.0)
  S1 = Momentary Switch [package=ksa_sealed_tac_switch]
  R2 = Resistor [tolerance=±5% resistance=220 package="1206 [SMD]"]

nets:
  N1: Componente1.GND, R2.Pin_1
  N2: Componente1.D2, S1.3
  N3: Componente1.5V, S1.2
  N4: S1.4, R2.Pin_0

// code stored in the sketch: pushbutton.ino

void setup() {
  pinMode(2, INPUT);
  Serial.begin(9600);
}

void loop() {
  // put your main code here, to run repeatedly:
 	int v= digitalRead (2);
  Serial.println(v);
}
